// Logisim project GameOfLife.circ as structural Verilog: 13 circuits, main circuit Main
// V
module Main (
);

  wire _1, _2, _3, button_2_out, button_out, cdm_1_change_state, Clear_out, keyboard_1_avail,
       \run_button_1_сonstant_signal , Run_out, speed_changer_1_game_speed, speed_changer_1_input_speed,
       speed_changer_1_pointer_speed;
  wire [3:0] coordinates_display_1_tens, coordinates_display_1_units, coordinates_display_2_tens,
       coordinates_display_2_units, s, x, y;
  wire [6:0] keyboard_1_data;
  wire [15:0] input_state_1_change_state_container, input_state_1_row, input_state_1_row_2,
       input_state_1_row_3, input_state_1_row_4, input_state_1_row_5, input_state_1_row_6,
       input_state_1_row_7, input_state_1_row_8, input_state_1_row_9, input_state_1_row_10,
       input_state_1_row_11, input_state_1_row_12, input_state_1_row_13, input_state_1_row_14,
       input_state_1_row_15, input_state_1_row_16, memory_1_output_row, memory_1_output_row_2,
       memory_1_output_row_3, memory_1_output_row_4, memory_1_output_row_5, memory_1_output_row_6,
       memory_1_output_row_7, memory_1_output_row_8, memory_1_output_row_9, memory_1_output_row_10,
       memory_1_output_row_11, memory_1_output_row_12, memory_1_output_row_13, memory_1_output_row_14,
       memory_1_output_row_15, memory_1_output_row_16;

  Input_State input_state_1 (
    .X(x), .Y(y), .Change_State(cdm_1_change_state), .Row(input_state_1_row), .Row_2(input_state_1_row_2),
    .Row_3(input_state_1_row_3), .Row_4(input_state_1_row_4), .Row_5(input_state_1_row_5),
    .Row_6(input_state_1_row_6), .Row_7(input_state_1_row_7), .Row_8(input_state_1_row_8),
    .Row_9(input_state_1_row_9), .Row_10(input_state_1_row_10), .Row_11(input_state_1_row_11),
    .Row_12(input_state_1_row_12), .Row_13(input_state_1_row_13), .Row_14(input_state_1_row_14),
    .Row_15(input_state_1_row_15), .Row_16(input_state_1_row_16),
    .Change_State_Container(input_state_1_change_state_container));
  Memory memory_1 (
    .Change_State(input_state_1_change_state_container), .Mode(\run_button_1_сonstant_signal ),
    .Output_row(memory_1_output_row), .Output_row_2(memory_1_output_row_2),
    .Output_row_3(memory_1_output_row_3), .Output_row_4(memory_1_output_row_4),
    .Output_row_5(memory_1_output_row_5), .Output_row_6(memory_1_output_row_6),
    .Output_row_7(memory_1_output_row_7), .Output_row_8(memory_1_output_row_8),
    .Output_row_9(memory_1_output_row_9), .Output_row_10(memory_1_output_row_10),
    .Output_row_11(memory_1_output_row_11), .Output_row_12(memory_1_output_row_12),
    .Output_row_13(memory_1_output_row_13), .Output_row_14(memory_1_output_row_14),
    .Output_row_15(memory_1_output_row_15), .Output_row_16(memory_1_output_row_16),
    .Pointer_clock(speed_changer_1_pointer_speed), .Game_clock(speed_changer_1_game_speed),
    .Clear(Clear_out), .Input_row_11(input_state_1_row_11), .Input_row_13(input_state_1_row_13),
    .Input_row_9(input_state_1_row_9), .Input_row_7(input_state_1_row_7), .Input_row_5(input_state_1_row_5),
    .Input_row_3(input_state_1_row_3), .Input_row(input_state_1_row), .Input_row_2(input_state_1_row_2),
    .Input_row_4(input_state_1_row_4), .Input_row_6(input_state_1_row_6),
    .Input_row_10(input_state_1_row_10), .Input_row_15(input_state_1_row_15),
    .Input_row_16(input_state_1_row_16), .Input_row_8(input_state_1_row_8),
    .Input_row_12(input_state_1_row_12), .Input_row_14(input_state_1_row_14));
  DotMatrix #(.inputtype("row"), .matrixcols(16), .matrixrows(16)) dotmatrix_1 (
    .row0(memory_1_output_row), .row1(memory_1_output_row_2), .row2(memory_1_output_row_3),
    .row3(memory_1_output_row_4), .row4(memory_1_output_row_5), .row5(memory_1_output_row_6),
    .row6(memory_1_output_row_7), .row7(memory_1_output_row_8), .row8(memory_1_output_row_9),
    .row9(memory_1_output_row_10), .row10(memory_1_output_row_11), .row11(memory_1_output_row_12),
    .row12(memory_1_output_row_13), .row13(memory_1_output_row_14), .row14(memory_1_output_row_15),
    .row15(memory_1_output_row_16));
  Run_button run_button_1 (.Button(Run_out), .\Сonstant_signal (\run_button_1_сonstant_signal ));
  Button Clear (.out(Clear_out));
  Keyboard #(.buflen(1), .trigger("falling")) keyboard_1 (
    .clk(speed_changer_1_input_speed), .avail(keyboard_1_avail), .data(keyboard_1_data));  // open: re, clr
  Speed_changer speed_changer_1 (
    .Input_speed(speed_changer_1_input_speed), .in_1(button_2_out), .in_2(button_out),
    .Game_speed(speed_changer_1_game_speed), .Pointer_speed(speed_changer_1_pointer_speed), .Speed_display(s));
  Button button (.out(button_out));
  Button button_2 (.out(button_2_out));
  Cdm cdm_1 (
    ._1(_1), ._2(_2), ._3(_3), .Change_State(cdm_1_change_state), .Was_changed(keyboard_1_avail), .X(x),
    .Y(y), .Run(\run_button_1_сonstant_signal ), .Input_key(keyboard_1_data));
  Button Run (.out(Run_out));
  Coordinates_display coordinates_display_1 (
    .Coordinate(x), .Tens(coordinates_display_1_tens), .Units(coordinates_display_1_units));
  Hex_Digit_Display hex_digit_display_1 (.value(coordinates_display_1_tens));  // open: dp
  Hex_Digit_Display hex_digit_display_2 (.value(coordinates_display_1_units));  // open: dp
  Hex_Digit_Display hex_digit_display_3 (.value(coordinates_display_2_tens));  // open: dp
  Button u__1 (.out(_1));
  Button u__2 (.out(_2));
  Button u__3 (.out(_3));
  Coordinates_display coordinates_display_2 (
    .Coordinate(y), .Tens(coordinates_display_2_tens), .Units(coordinates_display_2_units));
  Hex_Digit_Display hex_digit_display_4 (.value(s));  // open: dp
  Hex_Digit_Display hex_digit_display_5 (.value(coordinates_display_2_units));  // open: dp

  // Notes on the sheet:
  //   Control pointer
  //   Game of Life
  //   Pointer coordinates
  //   Pre-instaled shapes
  //   - create glider
  //   - create pulsar
  //   - create 4 gliders
  //   Speed
endmodule

module Cdm (
  input  Run,
  input  _1,
  input  _2,
  input  _3,
  input  Was_changed,
  input  [6:0] Input_key,
  output [3:0] Y,
  output [3:0] X,
  output Change_State
);

  wire and_1_out, and_2_out, and_4_out, cdm_8_mark5_1_data_inst, cdm_8_mark5_1_mem_cycle, clk,
       controlled_buffer_2_out, controlled_buffer_10_out, controlled_buffer_11_out, decoder_1_out0,
       decoder_1_out1, decoder_2_out0, decoder_2_out1, \default , \end , IOsel, nor_1_out, nor_2_out,
       not_1_out, not_2_out, not_3_out, not_4_out, not_5_out, one, pull_resistor_1_node,
       pull_resistor_2_node, pull_resistor_3_node, READwrite, three, two;
  wire [1:0] controlled_buffer_1_out, register_1_q;
  wire [3:0] cdm_8_mark5_1_ps, IOaddr;
  wire [6:0] controlled_buffer_14_out, register_2_q;
  wire [7:0] cdm_8_mark5_1_data_out, cdm_8_mark5_1_pc, cdm_8_mark5_1_r0, cdm_8_mark5_1_r1, cdm_8_mark5_1_r2,
       cdm_8_mark5_1_r3, controlled_buffer_13_out, IOdat;
  wire [7:4] cdm_8_mark5_1_addr;
  wire [7:7] s_r_ff_1_qn;

  not not_1 (not_1_out, Run);
  assign controlled_buffer_1_out = pull_resistor_2_node ? 2'b01 : 2'bz;  // Controlled_Buffer controlled_buffer_1
  Pull_Resistor pull_resistor_1 (.node(pull_resistor_1_node));
  Pull_Resistor pull_resistor_2 (.node(pull_resistor_2_node));
  assign controlled_buffer_2_out = pull_resistor_2_node ? pull_resistor_2_node : 1'bz;  // Controlled_Buffer controlled_buffer_2
  assign pull_resistor_2_node = not_1_out ? _1 : 1'bz;  // Controlled_Buffer controlled_buffer_3
  assign pull_resistor_1_node = not_1_out ? _2 : 1'bz;  // Controlled_Buffer controlled_buffer_4
  // Probe on cdm_8_mark5_1_r0
  // Probe on cdm_8_mark5_1_r1
  Clock clock_1 (.out(clk));
  and and_1 (and_1_out, IOsel, IOaddr[0], IOaddr[1], IOaddr[2], ~IOaddr[3]);  // AND_Gate
  and and_2 (and_2_out, IOsel, IOaddr[0], ~IOaddr[1], ~IOaddr[2], ~IOaddr[3]);  // AND_Gate
  assign controlled_buffer_1_out = pull_resistor_1_node ? 2'b10 : 2'bz;  // Controlled_Buffer controlled_buffer_5
  assign controlled_buffer_1_out = pull_resistor_3_node ? 2'b11 : 2'bz;  // Controlled_Buffer controlled_buffer_6
  Pull_Resistor pull_resistor_3 (.node(pull_resistor_3_node));
  assign controlled_buffer_2_out = pull_resistor_1_node ? pull_resistor_1_node : 1'bz;  // Controlled_Buffer controlled_buffer_7
  assign controlled_buffer_2_out = pull_resistor_3_node ? pull_resistor_3_node : 1'bz;  // Controlled_Buffer controlled_buffer_8
  assign pull_resistor_3_node = not_1_out ? _3 : 1'bz;  // Controlled_Buffer controlled_buffer_9
  // Probe on cdm_8_mark5_1_r2
  // Probe on cdm_8_mark5_1_pc
  // Probe on cdm_8_mark5_1_r3
  assign controlled_buffer_10_out = READwrite ? and_1_out : 1'bz;  // Controlled_Buffer controlled_buffer_10
  BitSelector #(.width(2)) bitselector_1 (.in(2'b10), .out(\end ), .sel(controlled_buffer_10_out));
  Pull_Resistor pull_resistor_4 (.node(\end ));
  assign controlled_buffer_11_out = READwrite ? and_2_out : 1'bz;  // Controlled_Buffer controlled_buffer_11
  BitSelector #(.width(2)) bitselector_2 (.in(2'b10), .out(Change_State), .sel(controlled_buffer_11_out));
  Pull_Resistor pull_resistor_5 (.node(Change_State));
  Demultiplexer #(.select(2), .enable("false")) demultiplexer_1 (
    .out0(\default ), .out1(one), .out2(two), .out3(three), .in(decoder_1_out0), .sel(register_1_q));
  Register #(.width(2)) register_1 (
    .D(controlled_buffer_1_out), .Q(register_1_q), .clk(controlled_buffer_2_out), .clr(\end ));  // open: en
  Pull_Resistor pull_resistor_6 (.node(controlled_buffer_2_out));
  // Probe on cdm_8_mark5_1_ps
  Decoder #(.disabled(0)) decoder_1 (
    .out0(decoder_1_out0), .out1(decoder_1_out1), .sel(cdm_8_mark5_1_data_inst), .en(cdm_8_mark5_1_mem_cycle));
  CdM_8_mark5 cdm_8_mark5_1 (
    .clock(clk), .addr({cdm_8_mark5_1_addr, IOaddr}), .mem_read(READwrite),
    .mem_cycle(cdm_8_mark5_1_mem_cycle), .data_inst(cdm_8_mark5_1_data_inst),
    .data_out(cdm_8_mark5_1_data_out), .data_in(controlled_buffer_13_out), .r0(cdm_8_mark5_1_r0),
    .r1(cdm_8_mark5_1_r1), .r2(cdm_8_mark5_1_r2), .r3(cdm_8_mark5_1_r3), .PC(cdm_8_mark5_1_pc),
    .PS(cdm_8_mark5_1_ps));  // open: SP
  not not_2 (not_2_out, READwrite);
  assign IOdat = not_2_out ? cdm_8_mark5_1_data_out : 8'bz;  // Controlled_Buffer controlled_buffer_12
  assign controlled_buffer_13_out = READwrite ? IOdat : 8'bz;  // Controlled_Buffer controlled_buffer_13
  and and_3 (IOsel, decoder_1_out1, cdm_8_mark5_1_addr[7], cdm_8_mark5_1_addr[6], cdm_8_mark5_1_addr[5], cdm_8_mark5_1_addr[4]);
  not not_3 (not_3_out, Was_changed);
  not not_4 (not_4_out, not_3_out);
  not not_5 (not_5_out, decoder_2_out1);
  assign controlled_buffer_14_out = Was_changed ? Input_key : 7'bz;  // Controlled_Buffer controlled_buffer_14
  Register #(.width(7), .trigger("falling")) register_2 (
    .D(controlled_buffer_14_out), .en(1'b1), .Q(register_2_q), .clk(not_3_out));  // open: clr
  nor nor_1 (nor_1_out, not_4_out, not_3_out);
  nor nor_2 (nor_2_out, not_5_out, decoder_2_out1);
  ROM rom_1 (.addr({cdm_8_mark5_1_addr, IOaddr}), .data(IOdat), .sel(three));
  ROM rom_2 (.addr({cdm_8_mark5_1_addr, IOaddr}), .data(IOdat), .sel(two));
  ROM rom_3 (.addr({cdm_8_mark5_1_addr, IOaddr}), .data(IOdat), .sel(one));
  ROM rom_4 (.addr({cdm_8_mark5_1_addr, IOaddr}), .data(IOdat), .sel(\default ));
  assign IOdat = decoder_2_out1 ? {s_r_ff_1_qn[7], register_2_q} : 8'bz;  // Controlled_Buffer controlled_buffer_15
  S_R_Flip_Flop #(.trigger("low")) s_r_ff_1 (
    .S(nor_1_out), .clk(1'b0), .R(nor_2_out), .Qn(s_r_ff_1_qn[7]));  // open: Q, preset, reset, en
  Register #(.trigger("falling")) register_3 (.D(IOdat), .en(decoder_2_out0), .Q({X, Y}), .clk(clk));  // open: clr
  Decoder #(.disabled(0)) decoder_2 (.out0(decoder_2_out0), .out1(decoder_2_out1), .sel(READwrite), .en(and_4_out));
  and and_4 (and_4_out, IOsel, IOaddr[0], IOaddr[1], ~IOaddr[2], ~IOaddr[3]);  // AND_Gate

  // Notes on the sheet:
  //   Buttons input
  //   Keyboard input
  //   contents of rom_1 (hex, n*v repeats v):
  //   d1 f7 a7 ee 20 27*0 d0 f3 d2 10 d3 0 6*1b 8f 8f 8f d1 3 5 e4 3e a3 d0 f1 a0 d0 f3 1b 89 ee 31 1b 8f
  //   8f 86 d1 7 5 e4 51 a3 d0 f1 a0 d0 f3 1b 89 ee 44 1b 8f 8f 86 d1 b 5 e4 64 a3 d0 f1 a0 d0 f3 1b 89 ee
  //   57 8f 8f 86 1b 1b 1b d1 7 5 e4 79 a3 d0 f1 a0 d0 f3 1b 89 ee 6c 8f 8f 86 1b 1b 1b d1 3 5 e4 8e a3 d0
  //   f1 a0 d0 f3 1b 89 ee 81 ee
  //   contents of rom_2 (hex, n*v repeats v):
  //   d1 f7 a7 ee 20 27*0 d0 f3 d2 10 d3 0 6*1b 8f 8f 8f d1 4 5 e4 3e a3 d0 f1 a0 d0 f3 1b 89 ee 31 1b 8f
  //   8f 86 d1 8 5 e4 51 a3 d0 f1 a0 d0 f3 1b 89 ee 44 1b 8f 8f 86 d1 c 5 e4 64 a3 d0 f1 a0 d0 f3 1b 89 ee
  //   57 8f 8f 86 1b 1b 1b d1 8 5 e4 79 a3 d0 f1 a0 d0 f3 1b 89 ee 6c 8f 8f 86 1b 1b 1b d1 4 5 e4 8e a3 d0
  //   f1 a0 d0 f3 1b 89 ee 81 ee
  //   contents of rom_3 (hex, n*v repeats v):
  //   d1 f7 a7 ee 20 27*0 d0 f3 d2 10 d3 0 8f 8f 8f 1b 1b a3 d0 f1 a0 d0 f3 8f a3 d0 f1 a0 d0 f3 8f a3 d0
  //   f1 a0 d0 f3 1b a3 d0 f1 a0 d0 f3 8b 1b a3 d0 f1 a0 d0 f3 ee
  //   contents of rom_4 (hex, n*v repeats v):
  //   d3 0 d2 1 d0 f3 b1 5 e4 6 d2 a 76 e1 16 d0 f1 a0 d0 f3 ee 6 d2 64 76 e1 21 d2 10 1b a3 ee 6 d2 61 76
  //   e1 2c d2 f0 1b a3 ee 6 d2 77 76 e1 40 e 4*96 a e1 3c d2 10 1b 8b a3 ee 6 d2 73 76 e1 56 e 4*96 d1 f0
  //   79 e1 52 d2 f0 1b 8f a3 ee 6 ee 6
  //   Pointer position
endmodule

module Input_State (
  input  [3:0] X,
  input  [3:0] Y,
  input  Change_State,
  output [15:0] Row,
  output [15:0] Row_2,
  output [15:0] Row_3,
  output [15:0] Row_4,
  output [15:0] Row_5,
  output [15:0] Row_6,
  output [15:0] Row_7,
  output [15:0] Row_8,
  output [15:0] Row_9,
  output [15:0] Row_10,
  output [15:0] Row_11,
  output [15:0] Row_12,
  output [15:0] Row_13,
  output [15:0] Row_14,
  output [15:0] Row_15,
  output [15:0] Row_16,
  output [15:0] Change_State_Container
);

  wire decoder_1_out0, decoder_1_out1, decoder_1_out2, decoder_1_out3, decoder_1_out4, decoder_1_out5,
       decoder_1_out6, decoder_1_out7, decoder_1_out8, decoder_1_out9, decoder_1_out10, decoder_1_out11,
       decoder_1_out12, decoder_1_out13, decoder_1_out14, decoder_1_out15, decoder_2_out0, decoder_2_out1,
       decoder_2_out2, decoder_2_out3, decoder_2_out4, decoder_2_out5, decoder_2_out6, decoder_2_out7,
       decoder_2_out8, decoder_2_out9, decoder_2_out10, decoder_2_out11, decoder_2_out12, decoder_2_out13,
       decoder_2_out14, decoder_2_out15;

  Decoder #(.select(4), .enable("false")) decoder_1 (
    .out0(decoder_1_out0), .out1(decoder_1_out1), .out2(decoder_1_out2), .out3(decoder_1_out3),
    .out4(decoder_1_out4), .out5(decoder_1_out5), .out6(decoder_1_out6), .out7(decoder_1_out7),
    .out8(decoder_1_out8), .out9(decoder_1_out9), .out10(decoder_1_out10), .out11(decoder_1_out11),
    .out12(decoder_1_out12), .out13(decoder_1_out13), .out14(decoder_1_out14), .out15(decoder_1_out15),
    .sel(Y));
  Decoder #(.select(4), .enable("false")) decoder_2 (
    .out0(decoder_2_out0), .out1(decoder_2_out1), .out2(decoder_2_out2), .out3(decoder_2_out3),
    .out4(decoder_2_out4), .out5(decoder_2_out5), .out6(decoder_2_out6), .out7(decoder_2_out7),
    .out8(decoder_2_out8), .out9(decoder_2_out9), .out10(decoder_2_out10), .out11(decoder_2_out11),
    .out12(decoder_2_out12), .out13(decoder_2_out13), .out14(decoder_2_out14), .out15(decoder_2_out15),
    .sel(X));
  Input input_1 (
    .Y(decoder_1_out0), .Change_State(Change_State), .Row(Row), .out_20(Change_State_Container[0]),
    .X(decoder_2_out0), .X_2(decoder_2_out1), .X_3(decoder_2_out2), .X_4(decoder_2_out3),
    .X_5(decoder_2_out4), .X_6(decoder_2_out5), .X_7(decoder_2_out6), .X_8(decoder_2_out7),
    .X_9(decoder_2_out8), .X_10(decoder_2_out9), .X_11(decoder_2_out10), .X_12(decoder_2_out11),
    .X_13(decoder_2_out12), .X_14(decoder_2_out13), .X_15(decoder_2_out14), .X_16(decoder_2_out15));
  Input input_2 (
    .Y(decoder_1_out1), .Change_State(Change_State), .Row(Row_2), .out_20(Change_State_Container[1]),
    .X(decoder_2_out0), .X_2(decoder_2_out1), .X_3(decoder_2_out2), .X_4(decoder_2_out3),
    .X_5(decoder_2_out4), .X_6(decoder_2_out5), .X_7(decoder_2_out6), .X_8(decoder_2_out7),
    .X_9(decoder_2_out8), .X_10(decoder_2_out9), .X_11(decoder_2_out10), .X_12(decoder_2_out11),
    .X_13(decoder_2_out12), .X_14(decoder_2_out13), .X_15(decoder_2_out14), .X_16(decoder_2_out15));
  Input input_3 (
    .Y(decoder_1_out2), .Change_State(Change_State), .Row(Row_3), .out_20(Change_State_Container[2]),
    .X(decoder_2_out0), .X_2(decoder_2_out1), .X_3(decoder_2_out2), .X_4(decoder_2_out3),
    .X_5(decoder_2_out4), .X_6(decoder_2_out5), .X_7(decoder_2_out6), .X_8(decoder_2_out7),
    .X_9(decoder_2_out8), .X_10(decoder_2_out9), .X_11(decoder_2_out10), .X_12(decoder_2_out11),
    .X_13(decoder_2_out12), .X_14(decoder_2_out13), .X_15(decoder_2_out14), .X_16(decoder_2_out15));
  Input input_4 (
    .Y(decoder_1_out3), .Change_State(Change_State), .Row(Row_4), .out_20(Change_State_Container[3]),
    .X(decoder_2_out0), .X_2(decoder_2_out1), .X_3(decoder_2_out2), .X_4(decoder_2_out3),
    .X_5(decoder_2_out4), .X_6(decoder_2_out5), .X_7(decoder_2_out6), .X_8(decoder_2_out7),
    .X_9(decoder_2_out8), .X_10(decoder_2_out9), .X_11(decoder_2_out10), .X_12(decoder_2_out11),
    .X_13(decoder_2_out12), .X_14(decoder_2_out13), .X_15(decoder_2_out14), .X_16(decoder_2_out15));
  Input input_5 (
    .Y(decoder_1_out4), .Change_State(Change_State), .Row(Row_5), .out_20(Change_State_Container[4]),
    .X(decoder_2_out0), .X_2(decoder_2_out1), .X_3(decoder_2_out2), .X_4(decoder_2_out3),
    .X_5(decoder_2_out4), .X_6(decoder_2_out5), .X_7(decoder_2_out6), .X_8(decoder_2_out7),
    .X_9(decoder_2_out8), .X_10(decoder_2_out9), .X_11(decoder_2_out10), .X_12(decoder_2_out11),
    .X_13(decoder_2_out12), .X_14(decoder_2_out13), .X_15(decoder_2_out14), .X_16(decoder_2_out15));
  Input input_6 (
    .Y(decoder_1_out5), .Change_State(Change_State), .Row(Row_6), .out_20(Change_State_Container[5]),
    .X(decoder_2_out0), .X_2(decoder_2_out1), .X_3(decoder_2_out2), .X_4(decoder_2_out3),
    .X_5(decoder_2_out4), .X_6(decoder_2_out5), .X_7(decoder_2_out6), .X_8(decoder_2_out7),
    .X_9(decoder_2_out8), .X_10(decoder_2_out9), .X_11(decoder_2_out10), .X_12(decoder_2_out11),
    .X_13(decoder_2_out12), .X_14(decoder_2_out13), .X_15(decoder_2_out14), .X_16(decoder_2_out15));
  Input input_7 (
    .Y(decoder_1_out6), .Change_State(Change_State), .Row(Row_7), .out_20(Change_State_Container[6]),
    .X(decoder_2_out0), .X_2(decoder_2_out1), .X_3(decoder_2_out2), .X_4(decoder_2_out3),
    .X_5(decoder_2_out4), .X_6(decoder_2_out5), .X_7(decoder_2_out6), .X_8(decoder_2_out7),
    .X_9(decoder_2_out8), .X_10(decoder_2_out9), .X_11(decoder_2_out10), .X_12(decoder_2_out11),
    .X_13(decoder_2_out12), .X_14(decoder_2_out13), .X_15(decoder_2_out14), .X_16(decoder_2_out15));
  Input input_8 (
    .Y(decoder_1_out7), .Change_State(Change_State), .Row(Row_8), .out_20(Change_State_Container[7]),
    .X(decoder_2_out0), .X_2(decoder_2_out1), .X_3(decoder_2_out2), .X_4(decoder_2_out3),
    .X_5(decoder_2_out4), .X_6(decoder_2_out5), .X_7(decoder_2_out6), .X_8(decoder_2_out7),
    .X_9(decoder_2_out8), .X_10(decoder_2_out9), .X_11(decoder_2_out10), .X_12(decoder_2_out11),
    .X_13(decoder_2_out12), .X_14(decoder_2_out13), .X_15(decoder_2_out14), .X_16(decoder_2_out15));
  Input input_9 (
    .Y(decoder_1_out8), .Change_State(Change_State), .Row(Row_9), .out_20(Change_State_Container[8]),
    .X(decoder_2_out0), .X_2(decoder_2_out1), .X_3(decoder_2_out2), .X_4(decoder_2_out3),
    .X_5(decoder_2_out4), .X_6(decoder_2_out5), .X_7(decoder_2_out6), .X_8(decoder_2_out7),
    .X_9(decoder_2_out8), .X_10(decoder_2_out9), .X_11(decoder_2_out10), .X_12(decoder_2_out11),
    .X_13(decoder_2_out12), .X_14(decoder_2_out13), .X_15(decoder_2_out14), .X_16(decoder_2_out15));
  Input input_10 (
    .Y(decoder_1_out9), .Change_State(Change_State), .Row(Row_10), .out_20(Change_State_Container[9]),
    .X(decoder_2_out0), .X_2(decoder_2_out1), .X_3(decoder_2_out2), .X_4(decoder_2_out3),
    .X_5(decoder_2_out4), .X_6(decoder_2_out5), .X_7(decoder_2_out6), .X_8(decoder_2_out7),
    .X_9(decoder_2_out8), .X_10(decoder_2_out9), .X_11(decoder_2_out10), .X_12(decoder_2_out11),
    .X_13(decoder_2_out12), .X_14(decoder_2_out13), .X_15(decoder_2_out14), .X_16(decoder_2_out15));
  Input input_11 (
    .Y(decoder_1_out10), .Change_State(Change_State), .Row(Row_11), .out_20(Change_State_Container[10]),
    .X(decoder_2_out0), .X_2(decoder_2_out1), .X_3(decoder_2_out2), .X_4(decoder_2_out3),
    .X_5(decoder_2_out4), .X_6(decoder_2_out5), .X_7(decoder_2_out6), .X_8(decoder_2_out7),
    .X_9(decoder_2_out8), .X_10(decoder_2_out9), .X_11(decoder_2_out10), .X_12(decoder_2_out11),
    .X_13(decoder_2_out12), .X_14(decoder_2_out13), .X_15(decoder_2_out14), .X_16(decoder_2_out15));
  Input input_12 (
    .Y(decoder_1_out11), .Change_State(Change_State), .Row(Row_12), .out_20(Change_State_Container[11]),
    .X(decoder_2_out0), .X_2(decoder_2_out1), .X_3(decoder_2_out2), .X_4(decoder_2_out3),
    .X_5(decoder_2_out4), .X_6(decoder_2_out5), .X_7(decoder_2_out6), .X_8(decoder_2_out7),
    .X_9(decoder_2_out8), .X_10(decoder_2_out9), .X_11(decoder_2_out10), .X_12(decoder_2_out11),
    .X_13(decoder_2_out12), .X_14(decoder_2_out13), .X_15(decoder_2_out14), .X_16(decoder_2_out15));
  Input input_13 (
    .Y(decoder_1_out12), .Change_State(Change_State), .Row(Row_13), .out_20(Change_State_Container[12]),
    .X(decoder_2_out0), .X_2(decoder_2_out1), .X_3(decoder_2_out2), .X_4(decoder_2_out3),
    .X_5(decoder_2_out4), .X_6(decoder_2_out5), .X_7(decoder_2_out6), .X_8(decoder_2_out7),
    .X_9(decoder_2_out8), .X_10(decoder_2_out9), .X_11(decoder_2_out10), .X_12(decoder_2_out11),
    .X_13(decoder_2_out12), .X_14(decoder_2_out13), .X_15(decoder_2_out14), .X_16(decoder_2_out15));
  Input input_14 (
    .Y(decoder_1_out13), .Change_State(Change_State), .Row(Row_14), .out_20(Change_State_Container[13]),
    .X(decoder_2_out0), .X_2(decoder_2_out1), .X_3(decoder_2_out2), .X_4(decoder_2_out3),
    .X_5(decoder_2_out4), .X_6(decoder_2_out5), .X_7(decoder_2_out6), .X_8(decoder_2_out7),
    .X_9(decoder_2_out8), .X_10(decoder_2_out9), .X_11(decoder_2_out10), .X_12(decoder_2_out11),
    .X_13(decoder_2_out12), .X_14(decoder_2_out13), .X_15(decoder_2_out14), .X_16(decoder_2_out15));
  Input input_15 (
    .Y(decoder_1_out14), .Change_State(Change_State), .Row(Row_15), .out_20(Change_State_Container[14]),
    .X(decoder_2_out0), .X_2(decoder_2_out1), .X_3(decoder_2_out2), .X_4(decoder_2_out3),
    .X_5(decoder_2_out4), .X_6(decoder_2_out5), .X_7(decoder_2_out6), .X_8(decoder_2_out7),
    .X_9(decoder_2_out8), .X_10(decoder_2_out9), .X_11(decoder_2_out10), .X_12(decoder_2_out11),
    .X_13(decoder_2_out12), .X_14(decoder_2_out13), .X_15(decoder_2_out14), .X_16(decoder_2_out15));
  Input input_16 (
    .Y(decoder_1_out15), .Change_State(Change_State), .Row(Row_16), .out_20(Change_State_Container[15]),
    .X(decoder_2_out0), .X_2(decoder_2_out1), .X_3(decoder_2_out2), .X_4(decoder_2_out3),
    .X_5(decoder_2_out4), .X_6(decoder_2_out5), .X_7(decoder_2_out6), .X_8(decoder_2_out7),
    .X_9(decoder_2_out8), .X_10(decoder_2_out9), .X_11(decoder_2_out10), .X_12(decoder_2_out11),
    .X_13(decoder_2_out12), .X_14(decoder_2_out13), .X_15(decoder_2_out14), .X_16(decoder_2_out15));

  // Other names for the same wires on the sheet: _0 = Change_State_Container[0]; _1 = Change_State_Container[1];
  //   _2 = Change_State_Container[2]; _3 = Change_State_Container[3]; _4 = Change_State_Container[4];
  //   _5 = Change_State_Container[5]; _6 = Change_State_Container[6]; _7 = Change_State_Container[7];
  //   _8 = Change_State_Container[8]; _9 = Change_State_Container[9]; _10 = Change_State_Container[10];
  //   _11 = Change_State_Container[11]; _12 = Change_State_Container[12]; _13 = Change_State_Container[13];
  //   _14 = Change_State_Container[14]; _15 = Change_State_Container[15]
endmodule

module Input (
  input  X,
  input  X_2,
  input  X_3,
  input  X_4,
  input  X_5,
  input  X_6,
  input  X_7,
  input  X_8,
  input  X_9,
  input  X_10,
  input  X_11,
  input  X_12,
  input  X_13,
  input  X_14,
  input  X_15,
  input  X_16,
  input  Y,
  input  Change_State,
  output [15:0] Row,
  output out_20
);

  wire or_1_out;

  and and_1 (Row[14], Y, X_2);
  and and_2 (Row[15], Y, X);
  and and_3 (Row[12], Y, X_4);
  and and_4 (Row[13], Y, X_3);
  and and_5 (Row[10], Y, X_6);
  and and_6 (Row[11], Y, X_5);
  and and_7 (Row[9], Y, X_7);
  and and_8 (Row[8], Y, X_8);
  and and_9 (Row[6], Y, X_10);
  and and_10 (Row[7], Y, X_9);
  and and_11 (Row[4], Y, X_12);
  and and_12 (Row[5], Y, X_11);
  and and_13 (Row[2], Y, X_14);
  and and_14 (Row[3], Y, X_13);
  and and_15 (Row[0], Y, X_16);
  and and_16 (Row[1], Y, X_15);
  or or_1 (or_1_out, Row[0], Row[1], Row[2], Row[3], Row[4], Row[5], Row[6], Row[7], Row[8], Row[9], Row[10], Row[11], Row[12], Row[13], Row[14], Row[15], 1'b0);
  and and_17 (out_20, or_1_out, Change_State);

  // Notes on the sheet:
  //   Row: pull=down
endmodule

module Memory (
  input  Mode,
  input  Pointer_clock,
  input  Game_clock,
  input  [15:0] Change_State,
  input  Clear,
  input  [15:0] Input_row,
  input  [15:0] Input_row_2,
  input  [15:0] Input_row_3,
  input  [15:0] Input_row_4,
  input  [15:0] Input_row_5,
  input  [15:0] Input_row_6,
  input  [15:0] Input_row_7,
  input  [15:0] Input_row_8,
  input  [15:0] Input_row_9,
  input  [15:0] Input_row_10,
  input  [15:0] Input_row_11,
  input  [15:0] Input_row_12,
  input  [15:0] Input_row_13,
  input  [15:0] Input_row_14,
  input  [15:0] Input_row_15,
  input  [15:0] Input_row_16,
  output [15:0] Output_row,
  output [15:0] Output_row_2,
  output [15:0] Output_row_3,
  output [15:0] Output_row_4,
  output [15:0] Output_row_5,
  output [15:0] Output_row_6,
  output [15:0] Output_row_7,
  output [15:0] Output_row_8,
  output [15:0] Output_row_9,
  output [15:0] Output_row_10,
  output [15:0] Output_row_11,
  output [15:0] Output_row_12,
  output [15:0] Output_row_13,
  output [15:0] Output_row_14,
  output [15:0] Output_row_15,
  output [15:0] Output_row_16
);

  wire Cl, cl_t, is;
  wire [15:0] down, rows_producer_1_middle_row_for_lower, rows_producer_2_middle_row_for_lower,
       rows_producer_2_middle_row_for_upper, rows_producer_3_middle_row_for_lower,
       rows_producer_3_middle_row_for_upper, rows_producer_4_middle_row_for_lower,
       rows_producer_4_middle_row_for_upper, rows_producer_5_middle_row_for_lower,
       rows_producer_5_middle_row_for_upper, rows_producer_6_middle_row_for_lower,
       rows_producer_6_middle_row_for_upper, rows_producer_7_middle_row_for_lower,
       rows_producer_7_middle_row_for_upper, rows_producer_8_middle_row_for_lower,
       rows_producer_8_middle_row_for_upper, rows_producer_9_middle_row_for_lower,
       rows_producer_9_middle_row_for_upper, rows_producer_10_middle_row_for_lower,
       rows_producer_10_middle_row_for_upper, rows_producer_11_middle_row_for_lower,
       rows_producer_11_middle_row_for_upper, rows_producer_12_middle_row_for_lower,
       rows_producer_12_middle_row_for_upper, rows_producer_13_middle_row_for_lower,
       rows_producer_13_middle_row_for_upper, rows_producer_14_middle_row_for_lower,
       rows_producer_14_middle_row_for_upper, rows_producer_15_middle_row_for_lower,
       rows_producer_15_middle_row_for_upper, rows_producer_16_middle_row_for_upper, up;

  Multiplexer #(.enable("false")) multiplexer_1 (.in0(Pointer_clock), .in1(Game_clock), .out(cl_t), .sel(Mode));
  not not_1 (is, Mode);
  assign Cl = Mode ? cl_t : 1'bz;  // Controlled_Buffer controlled_buffer_1
  Pull_Resistor pull_resistor_1 (.node(Cl));
  Rows_producer rows_producer_1 (
    .Input_row(Input_row), .Change_state(Change_State[0]), .Result_row(Output_row), .cl(cl_t), .Mode(is),
    .Cl_2(Cl), .Lower_row(rows_producer_2_middle_row_for_upper), .Middle_row_for_upper(up), .Upper_row(down),
    .Middle_row_for_lower(rows_producer_1_middle_row_for_lower), .Clear(Clear));
  Rows_producer rows_producer_2 (
    .Input_row(Input_row_2), .Change_state(Change_State[1]), .Result_row(Output_row_2), .cl(cl_t), .Mode(is),
    .Cl_2(Cl), .Lower_row(rows_producer_3_middle_row_for_upper),
    .Middle_row_for_upper(rows_producer_2_middle_row_for_upper),
    .Upper_row(rows_producer_1_middle_row_for_lower),
    .Middle_row_for_lower(rows_producer_2_middle_row_for_lower), .Clear(Clear));
  Rows_producer rows_producer_3 (
    .Input_row(Input_row_3), .Change_state(Change_State[2]), .Result_row(Output_row_3), .cl(cl_t), .Mode(is),
    .Cl_2(Cl), .Lower_row(rows_producer_4_middle_row_for_upper),
    .Middle_row_for_upper(rows_producer_3_middle_row_for_upper),
    .Upper_row(rows_producer_2_middle_row_for_lower),
    .Middle_row_for_lower(rows_producer_3_middle_row_for_lower), .Clear(Clear));
  Rows_producer rows_producer_4 (
    .Input_row(Input_row_4), .Change_state(Change_State[3]), .Result_row(Output_row_4), .cl(cl_t), .Mode(is),
    .Cl_2(Cl), .Lower_row(rows_producer_5_middle_row_for_upper),
    .Middle_row_for_upper(rows_producer_4_middle_row_for_upper),
    .Upper_row(rows_producer_3_middle_row_for_lower),
    .Middle_row_for_lower(rows_producer_4_middle_row_for_lower), .Clear(Clear));
  Rows_producer rows_producer_5 (
    .Input_row(Input_row_5), .Change_state(Change_State[4]), .Result_row(Output_row_5), .cl(cl_t), .Mode(is),
    .Cl_2(Cl), .Lower_row(rows_producer_6_middle_row_for_upper),
    .Middle_row_for_upper(rows_producer_5_middle_row_for_upper),
    .Upper_row(rows_producer_4_middle_row_for_lower),
    .Middle_row_for_lower(rows_producer_5_middle_row_for_lower), .Clear(Clear));
  Rows_producer rows_producer_6 (
    .Input_row(Input_row_6), .Change_state(Change_State[5]), .Result_row(Output_row_6), .cl(cl_t), .Mode(is),
    .Cl_2(Cl), .Lower_row(rows_producer_7_middle_row_for_upper),
    .Middle_row_for_upper(rows_producer_6_middle_row_for_upper),
    .Upper_row(rows_producer_5_middle_row_for_lower),
    .Middle_row_for_lower(rows_producer_6_middle_row_for_lower), .Clear(Clear));
  Rows_producer rows_producer_7 (
    .Input_row(Input_row_7), .Change_state(Change_State[6]), .Result_row(Output_row_7), .cl(cl_t), .Mode(is),
    .Cl_2(Cl), .Lower_row(rows_producer_8_middle_row_for_upper),
    .Middle_row_for_upper(rows_producer_7_middle_row_for_upper),
    .Upper_row(rows_producer_6_middle_row_for_lower),
    .Middle_row_for_lower(rows_producer_7_middle_row_for_lower), .Clear(Clear));
  Rows_producer rows_producer_8 (
    .Input_row(Input_row_8), .Change_state(Change_State[7]), .Result_row(Output_row_8), .cl(cl_t), .Mode(is),
    .Cl_2(Cl), .Lower_row(rows_producer_9_middle_row_for_upper),
    .Middle_row_for_upper(rows_producer_8_middle_row_for_upper),
    .Upper_row(rows_producer_7_middle_row_for_lower),
    .Middle_row_for_lower(rows_producer_8_middle_row_for_lower), .Clear(Clear));
  Rows_producer rows_producer_9 (
    .Input_row(Input_row_9), .Change_state(Change_State[8]), .Result_row(Output_row_9), .cl(cl_t), .Mode(is),
    .Cl_2(Cl), .Lower_row(rows_producer_10_middle_row_for_upper),
    .Middle_row_for_upper(rows_producer_9_middle_row_for_upper),
    .Upper_row(rows_producer_8_middle_row_for_lower),
    .Middle_row_for_lower(rows_producer_9_middle_row_for_lower), .Clear(Clear));
  Rows_producer rows_producer_10 (
    .Input_row(Input_row_10), .Change_state(Change_State[9]), .Result_row(Output_row_10), .cl(cl_t),
    .Mode(is), .Cl_2(Cl), .Lower_row(rows_producer_11_middle_row_for_upper),
    .Middle_row_for_upper(rows_producer_10_middle_row_for_upper),
    .Upper_row(rows_producer_9_middle_row_for_lower),
    .Middle_row_for_lower(rows_producer_10_middle_row_for_lower), .Clear(Clear));
  Rows_producer rows_producer_11 (
    .Input_row(Input_row_11), .Change_state(Change_State[10]), .Result_row(Output_row_11), .cl(cl_t),
    .Mode(is), .Cl_2(Cl), .Lower_row(rows_producer_12_middle_row_for_upper),
    .Middle_row_for_upper(rows_producer_11_middle_row_for_upper),
    .Upper_row(rows_producer_10_middle_row_for_lower),
    .Middle_row_for_lower(rows_producer_11_middle_row_for_lower), .Clear(Clear));
  Rows_producer rows_producer_12 (
    .Input_row(Input_row_12), .Change_state(Change_State[11]), .Result_row(Output_row_12), .cl(cl_t),
    .Mode(is), .Cl_2(Cl), .Lower_row(rows_producer_13_middle_row_for_upper),
    .Middle_row_for_upper(rows_producer_12_middle_row_for_upper),
    .Upper_row(rows_producer_11_middle_row_for_lower),
    .Middle_row_for_lower(rows_producer_12_middle_row_for_lower), .Clear(Clear));
  Rows_producer rows_producer_13 (
    .Input_row(Input_row_13), .Change_state(Change_State[12]), .Result_row(Output_row_13), .cl(cl_t),
    .Mode(is), .Cl_2(Cl), .Lower_row(rows_producer_14_middle_row_for_upper),
    .Middle_row_for_upper(rows_producer_13_middle_row_for_upper),
    .Upper_row(rows_producer_12_middle_row_for_lower),
    .Middle_row_for_lower(rows_producer_13_middle_row_for_lower), .Clear(Clear));
  Rows_producer rows_producer_14 (
    .Input_row(Input_row_14), .Change_state(Change_State[13]), .Result_row(Output_row_14), .cl(cl_t),
    .Mode(is), .Cl_2(Cl), .Lower_row(rows_producer_15_middle_row_for_upper),
    .Middle_row_for_upper(rows_producer_14_middle_row_for_upper),
    .Upper_row(rows_producer_13_middle_row_for_lower),
    .Middle_row_for_lower(rows_producer_14_middle_row_for_lower), .Clear(Clear));
  Rows_producer rows_producer_15 (
    .Input_row(Input_row_15), .Change_state(Change_State[14]), .Result_row(Output_row_15), .cl(cl_t),
    .Mode(is), .Cl_2(Cl), .Lower_row(rows_producer_16_middle_row_for_upper),
    .Middle_row_for_upper(rows_producer_15_middle_row_for_upper),
    .Upper_row(rows_producer_14_middle_row_for_lower),
    .Middle_row_for_lower(rows_producer_15_middle_row_for_lower), .Clear(Clear));
  Rows_producer rows_producer_16 (
    .Input_row(Input_row_16), .Change_state(Change_State[15]), .Result_row(Output_row_16), .cl(cl_t),
    .Mode(is), .Cl_2(Cl), .Lower_row(up), .Middle_row_for_upper(rows_producer_16_middle_row_for_upper),
    .Upper_row(rows_producer_15_middle_row_for_lower), .Middle_row_for_lower(down), .Clear(Clear));
endmodule

module Rows_producer (
  input  cl,
  input  [15:0] Input_row,
  input  Mode,
  input  Clear,
  input  Cl_2,
  input  [15:0] Upper_row,
  input  Change_state,
  input  [15:0] Lower_row,
  output [15:0] Result_row,
  output [15:0] Middle_row_for_lower,
  output [15:0] Middle_row_for_upper
);

  wire pointer_delay_1_delay_cl, pull_resistor_2_node;
  wire [15:0] controlled_buffer_1_out, controlled_buffer_2_out, multiplexer_1_out, \new , xor_1_out;
  wire [17:0] converter_16_to_18_1__18, converter_16_to_18_2__18, converter_16_to_18_3__18;

  assign controlled_buffer_1_out = cl ? Input_row : 16'bz;  // Controlled_Buffer controlled_buffer_1
  assign xor_1_out = Middle_row_for_lower ^ Input_row;  // XOR_Gate xor_1, 16 bits wide
  Pointer_delay pointer_delay_1 (.delay_Cl(pointer_delay_1_delay_cl), .Mode(Mode), .Cl(Cl_2));
  assign controlled_buffer_2_out = Mode ? controlled_buffer_1_out : 16'bz;  // Controlled_Buffer controlled_buffer_2
  Pull_Resistor pull_resistor_1 (.node(controlled_buffer_2_out));
  Register #(.width(16)) register_1 (
    .D(multiplexer_1_out), .Q(Middle_row_for_lower), .clk(pull_resistor_2_node), .clr(Clear));  // open: en
  Multiplexer #(.width(16), .enable("false")) multiplexer_1 (
    .in0(\new ), .in1(xor_1_out), .out(multiplexer_1_out), .sel(Mode));
  Pull_Resistor pull_resistor_2 (.node(pull_resistor_2_node));
  assign pull_resistor_2_node = pointer_delay_1_delay_cl ? Cl_2 : 1'bz;  // Controlled_Buffer controlled_buffer_3
  assign pull_resistor_2_node = Change_state ? Change_state : 1'bz;  // Controlled_Buffer controlled_buffer_4
  assign Result_row = controlled_buffer_2_out ^ Middle_row_for_lower;  // XOR_Gate xor_2, 16 bits wide
  Converter_16_to_18 converter_16_to_18_1 (._16(Upper_row), ._18(converter_16_to_18_1__18));
  Converter_16_to_18 converter_16_to_18_2 (._16(Middle_row_for_lower), ._18(converter_16_to_18_2__18));
  Converter_16_to_18 converter_16_to_18_3 (._16(Lower_row), ._18(converter_16_to_18_3__18));
  One_row_logic one_row_logic_1 (
    .Upper_row(converter_16_to_18_1__18), .Middle_row(converter_16_to_18_2__18),
    .Lower_row(converter_16_to_18_3__18), .Row_with_game_logic(\new ));

  assign Middle_row_for_upper = Middle_row_for_lower;

  // Notes on the sheet:
  //   pointer
  //   field
  //   Logic applying
endmodule

// delay
module Pointer_delay (
  input  Cl,
  input  Mode,
  output delay_Cl
);

  wire [1:0] counter_1_q;

  Counter #(.width(2), .max('h3), .ongoal("stay")) counter_1 (
    .Q(counter_1_q), .clk(Cl), .clr(Mode));  // open: load, D, count, carry
  and and_1 (delay_Cl, counter_1_q[0], counter_1_q[1]);
endmodule

module Converter_16_to_18 (
  input  [15:0] _16,
  output [17:0] _18
);


  assign _18 = {_16[0], _16, _16[15]};
endmodule

// Row logic
module One_row_logic (
  input  [17:0] Upper_row,
  input  [17:0] Middle_row,
  input  [17:0] Lower_row,
  output [15:0] Row_with_game_logic
);

  One_cell_logic one_cell_logic_1 (
    .Result_cell(Row_with_game_logic[0]), .Container({Lower_row[2:0], Middle_row[2:0], Upper_row[2:0]}));
  One_cell_logic one_cell_logic_2 (
    .Result_cell(Row_with_game_logic[1]), .Container({Lower_row[3:1], Middle_row[3:1], Upper_row[3:1]}));
  One_cell_logic one_cell_logic_3 (
    .Result_cell(Row_with_game_logic[2]), .Container({Lower_row[4:2], Middle_row[4:2], Upper_row[4:2]}));
  One_cell_logic one_cell_logic_4 (
    .Result_cell(Row_with_game_logic[3]), .Container({Lower_row[5:3], Middle_row[5:3], Upper_row[5:3]}));
  One_cell_logic one_cell_logic_5 (
    .Result_cell(Row_with_game_logic[4]), .Container({Lower_row[6:4], Middle_row[6:4], Upper_row[6:4]}));
  One_cell_logic one_cell_logic_6 (
    .Result_cell(Row_with_game_logic[5]), .Container({Lower_row[7:5], Middle_row[7:5], Upper_row[7:5]}));
  One_cell_logic one_cell_logic_7 (
    .Result_cell(Row_with_game_logic[6]), .Container({Lower_row[8:6], Middle_row[8:6], Upper_row[8:6]}));
  One_cell_logic one_cell_logic_8 (
    .Result_cell(Row_with_game_logic[7]), .Container({Lower_row[9:7], Middle_row[9:7], Upper_row[9:7]}));
  One_cell_logic one_cell_logic_9 (
    .Result_cell(Row_with_game_logic[8]), .Container({Lower_row[10:8], Middle_row[10:8], Upper_row[10:8]}));
  One_cell_logic one_cell_logic_10 (
    .Result_cell(Row_with_game_logic[9]), .Container({Lower_row[11:9], Middle_row[11:9], Upper_row[11:9]}));
  One_cell_logic one_cell_logic_11 (
    .Result_cell(Row_with_game_logic[10]), .Container({Lower_row[12:10], Middle_row[12:10], Upper_row[12:10]}));
  One_cell_logic one_cell_logic_12 (
    .Result_cell(Row_with_game_logic[11]), .Container({Lower_row[13:11], Middle_row[13:11], Upper_row[13:11]}));
  One_cell_logic one_cell_logic_13 (
    .Result_cell(Row_with_game_logic[12]), .Container({Lower_row[14:12], Middle_row[14:12], Upper_row[14:12]}));
  One_cell_logic one_cell_logic_14 (
    .Result_cell(Row_with_game_logic[13]), .Container({Lower_row[15:13], Middle_row[15:13], Upper_row[15:13]}));
  One_cell_logic one_cell_logic_15 (
    .Result_cell(Row_with_game_logic[14]), .Container({Lower_row[16:14], Middle_row[16:14], Upper_row[16:14]}));
  One_cell_logic one_cell_logic_16 (
    .Result_cell(Row_with_game_logic[15]), .Container({Lower_row[17:15], Middle_row[17:15], Upper_row[17:15]}));

  // Other names for the same wires on the sheet: up[17:0] = Upper_row; mid[17:0] = Middle_row; low[17:0] = Lower_row
endmodule

// Cell
module One_cell_logic (
  input  [8:0] Container,
  output Result_cell
);

  wire comparator_1_eq, comparator_1_gt, comparator_2_eq, comparator_2_gt;
  wire [1:0] adder_1_out, adder_2_out, adder_3_out, adder_4_out, adder_5_out, adder_6_out;
  wire [2:0] adder_7_out;
  wire [2:2] adder_5_cout, adder_6_cout;
  wire [3:3] adder_7_cout;

  Adder #(.width(1)) adder_1 (
    .a(Container[0]), .b(Container[1]), .out(adder_1_out[0]), .cout(adder_1_out[1]));  // open: cin
  Adder #(.width(1)) adder_2 (
    .a(Container[2]), .b(Container[3]), .out(adder_2_out[0]), .cout(adder_2_out[1]));  // open: cin
  Adder #(.width(1)) adder_3 (
    .a(Container[8]), .b(Container[5]), .out(adder_3_out[0]), .cout(adder_3_out[1]));  // open: cin
  Adder #(.width(1)) adder_4 (
    .a(Container[6]), .b(Container[7]), .out(adder_4_out[0]), .cout(adder_4_out[1]));  // open: cin
  Adder #(.width(2)) adder_5 (
    .a(adder_1_out), .b(adder_2_out), .out(adder_5_out), .cout(adder_5_cout[2]));  // open: cin
  Adder #(.width(2)) adder_6 (
    .a(adder_3_out), .b(adder_4_out), .out(adder_6_out), .cout(adder_6_cout[2]));  // open: cin
  Adder #(.width(3)) adder_7 (
    .a({adder_5_cout[2], adder_5_out}), .b({adder_6_cout[2], adder_6_out}), .out(adder_7_out),
    .cout(adder_7_cout[3]));  // open: cin
  Comparator #(.width(4), .mode("unsigned")) comparator_1 (
    .a({adder_7_cout[3], adder_7_out}), .b(4'b0011), .gt(comparator_1_gt), .eq(comparator_1_eq));  // open: lt
  Comparator #(.width(4), .mode("unsigned")) comparator_2 (
    .a(4'b0010), .b({adder_7_cout[3], adder_7_out}), .gt(comparator_2_gt), .eq(comparator_2_eq));  // open: lt
  assign Result_cell = comparator_1_gt ? 1'b0 : 1'bz;  // Controlled_Buffer controlled_buffer_1
  assign Result_cell = comparator_1_eq ? 1'b1 : 1'bz;  // Controlled_Buffer controlled_buffer_2
  assign Result_cell = comparator_2_gt ? 1'b0 : 1'bz;  // Controlled_Buffer controlled_buffer_3
  assign Result_cell = comparator_2_eq ? Container[4] : 1'bz;  // Controlled_Buffer controlled_buffer_4

  // Notes on the sheet:
  //   bordering cells
  //   current cell
endmodule

// Pointer coordinate
module Coordinates_display (
  input  [3:0] Coordinate,
  output [3:0] Tens,
  output [3:0] Units
);

  wire comparator_1_lt;
  wire [3:0] adder_1_out;

  Comparator #(.width(4), .mode("unsigned")) comparator_1 (
    .a(4'b1001), .b(Coordinate), .lt(comparator_1_lt));  // open: gt, eq
  Adder #(.width(4)) adder_1 (.a(Coordinate), .b(4'b0110), .out(adder_1_out));  // open: cin, cout
  assign Tens = {{3{1'b0}}, comparator_1_lt};  // Bit_Extender bit_extender_1
  Multiplexer #(.width(4)) multiplexer_1 (
    .in0(Coordinate), .in1(adder_1_out), .out(Units), .sel(comparator_1_lt));  // open: en
endmodule

module Speed_changer (
  input  in_1,
  input  in_2,
  output Input_speed,
  output Game_speed,
  output Pointer_speed,
  output [3:0] Speed_display
);

  wire clock_1_out, clock_3_out, clock_4_out, controlled_buffer_1_out;
  wire [1:0] counter_1_q;

  assign controlled_buffer_1_out = in_1 ? in_1 : 1'bz;  // Controlled_Buffer controlled_buffer_1
  Pull_Resistor pull_resistor_1 (.node(controlled_buffer_1_out));
  assign controlled_buffer_1_out = in_2 ? in_2 : 1'bz;  // Controlled_Buffer controlled_buffer_2
  Clock #(.highDuration(30), .lowDuration(30)) clock_1 (.out(clock_1_out));
  Counter #(.width(2), .max('h3), .ongoal("stay")) counter_1 (
    .load(in_1), .count(1'b1), .Q(counter_1_q), .clk(controlled_buffer_1_out));  // open: D, carry, clr
  assign Speed_display = {{2{1'b0}}, counter_1_q};  // Bit_Extender bit_extender_1
  Clock #(.highDuration(5), .lowDuration(5)) clock_2 (.out(Input_speed));
  Clock #(.highDuration(10), .lowDuration(10)) clock_3 (.out(clock_3_out));
  Clock #(.highDuration(20), .lowDuration(20)) clock_4 (.out(clock_4_out));
  Multiplexer #(.select(2), .enable("false")) multiplexer_1 (
    .in0(clock_1_out), .in1(clock_4_out), .in2(clock_3_out), .in3(Input_speed), .out(Game_speed),
    .sel(counter_1_q));
  Clock #(.highDuration(100), .lowDuration(100)) clock_5 (.out(Pointer_speed));

  // Notes on the sheet:
  //   2
  //   1
  //   0
  //   3
endmodule

module Run_button (
  input  Button,
  output \Сonstant_signal 
);

  Counter #(.width(1), .max('h1)) counter_1 (.Q(\Сonstant_signal ), .clk(Button));  // open: load, D, count, carry, clr
endmodule
